# Fritzing sketch _2buttons_servo2 (saved by Fritzing 0.9.3b)
breadboards: 1

parts:
  Part1 = Arduino Uno (Rev3)
  J1 = Basic Servo
  VCC1 = 4 x AAA Battery Mount
  S1 = Round Pushbutton
  S2 = Round Pushbutton

nets:
  N1: Part1.D10_PWM/SS, J1.pulse
  GND: Part1.GND, J1.gnd, VCC1.-, S1.leg1, S2.leg1
  N2: Part1.D3_PWM, S1.leg0
  N3: Part1.D4, S2.leg0
  N4: J1.vcc, VCC1.+
